// Logisim project circuitoMult.circ as structural Verilog: 1 circuit, main circuit main
module main (
  input  A0,
  input  A1,
  input  B0,
  input  B1,
  output R0,
  output R1,
  output R2,
  output R3
);

  wire and_2_out, and_3_out, and_4_out, and_5_out, and_6_out, and_7_out, not_1_out, not_2_out, not_3_out,
       not_4_out, not_5_out, not_6_out;

  and and_1 (R0, A0, B0);
  not not_1 (not_1_out, A0);
  and and_2 (and_2_out, not_1_out, A1, B0);
  and and_3 (and_3_out, A1, B0, not_2_out);
  not not_2 (not_2_out, B1);
  not not_3 (not_3_out, A1);
  and and_4 (and_4_out, A0, not_3_out, B1);
  and and_5 (and_5_out, A0, not_4_out, B1);
  not not_4 (not_4_out, B0);
  not not_5 (not_5_out, A0);
  and and_6 (and_6_out, not_5_out, A1, B1);
  not not_6 (not_6_out, B0);
  and and_7 (and_7_out, A1, not_6_out, B1);
  and and_8 (R3, A0, A1, B0, B1);
  or or_1 (R1, and_2_out, and_3_out, and_4_out, and_5_out);
  or or_2 (R2, and_6_out, and_7_out);
endmodule
